# Fritzing sketch FranzininhoWiFi_LCD_16X2_I2C_Fritzing (saved by Fritzing 0.9.6b)
breadboards: 1

parts:
  Part1 = Franzininho WiFi
  Part2 = LCD1602-I2C

nets:
  N1: Part1.8, Part2.SDA
  N2: Part1.9, Part2.SCL
  N3: Part1.GND#19, Part2.GND
  3V3: Part1.3V3, Part2.VCC

custom parts:
  Franzininho WiFi: Placa de desenvolvimento ESP32-S2
  LCD1602-I2C: A standard character display, usually with 2x16 characters. Comes in many colors with LCM1602 IIC attached.
