# Fritzing sketch FranzininhoWiFi_ST7789_240x240_Fritzing (saved by Fritzing 0.9.6b)
breadboards: 1

parts:
  A1 = lcd color display 1.3in 240x240 7pin interface [package=THT]
  Part1 = Franzininho WiFi
  S1 = Pushbutton [package="[THT]"]

nets:
  N1: A1.GND, Part1.GND#19, S1.Pin_1, S1.Pin_2
  VCC: A1.VCC, Part1.3V3
  N2: A1.SCL, Part1.12
  N3: A1.SDA, Part1.13
  N4: A1.RES, Part1.14
  N5: A1.DC, Part1.15
  N6: A1.BLK, Part1.16
  N7: Part1.3, S1.Pin_3, S1.Pin_4

custom parts:
  lcd color display 1.3in 240x240 7pin interface: 1.3 Inch Color 240 x 240 IPS TFT LCD Display Screen Module Board 7 Pin 4 Wire ST7789VW Drive IC SPI interface.
  Franzininho WiFi: Placa de desenvolvimento ESP32-S2
