# Fritzing sketch FranzininhoWiFi_OLED_Fritzing (saved by Fritzing 0.9.6b)
breadboards: 1

parts:
  Part1 = Franzininho WiFi
  OLED_I2C1 = OLED 128x64 I2C Monochrome Display

nets:
  N1: Part1.8, OLED_I2C1.SDA
  N2: Part1.9, OLED_I2C1.SCK
  N3: Part1.GND#19, OLED_I2C1.GND
  3V3: Part1.3V3, OLED_I2C1.VDD

custom parts:
  Franzininho WiFi: Placa de desenvolvimento ESP32-S2
