# Fritzing sketch FranzininhoWiFi_NeoPixel (saved by Fritzing 0.9.6b)
breadboards: 1

parts:
  LED1 = Super Flux RGB LED (com. anode)
  Part1 = Franzininho WiFi

nets:
  N1: LED1.blue_cathode, Part1.GND#24
  N2: LED1.green_cathode, Part1.18
  N3: LED1.common_anode, Part1.5V

custom parts:
  Franzininho WiFi: Placa de desenvolvimento ESP32-S2
