# Fritzing sketch FranzininhoWiFi_DC_Motor (saved by Fritzing 0.9.6b)
breadboards: 1

parts:
  S1 = H-Bridge with L298N
  Part1 = Franzininho WiFi
  J1 = Power Jack [package=power_jack_pth_lock]
  M1 = DC Motor

nets:
  N1: S1.12V, J1.PWR
  N2: S1.GND, Part1.GND#19, J1.GNDBREAK
  N3: S1.IN3, Part1.2
  N4: S1.IN4, Part1.1
  N5: S1.M2-01, M1.pin_2
  N6: S1.M2-02, M1.pin_1

custom parts:
  H-Bridge with L298N: h-bridge
  Franzininho WiFi: Placa de desenvolvimento ESP32-S2
