# Fritzing sketch FranzininhoWiFi_DHT_Fritizing (saved by Fritzing 0.9.6b)
breadboards: 1

parts:
  DHT1 = DHT22 Humidity and Temperature Sensor
  Part1 = Franzininho WiFi
  R1 = Resistor [tolerance=±5% power=0.25 resistance=4.7k package=THT]

nets:
  VDD: DHT1.VDD, Part1.3V3, R1.Pin_0
  N1: DHT1.DATA, Part1.4, R1.Pin_1
  N2: DHT1.GND, Part1.GND#19

custom parts:
  Franzininho WiFi: Placa de desenvolvimento ESP32-S2
