# Fritzing sketch FranzininhoWiFi_DS18B20_Fritzing (saved by Fritzing 0.9.6b)
breadboards: 1

parts:
  Part1 = franzininho-wifi-ESP32-S2
  DS1 = DS18B20 1-Wire Temperature Sensor [part_number=DS18B20]
  R1 = Resistor [tolerance=±5% power=0.25 resistance=4.7k package=THT]

nets:
  N1: Part1.connector4, DS1.DQ, R1.Pin_0
  N2: Part1.connector20, DS1.GND, R1.Pin_1
