# Fritzing sketch FranzininhoWiFi_MPU6050_Fritzing (saved by Fritzing 0.9.6b)
breadboards: 1

parts:
  GY1 = GY-521 (MPU-6050) [form="♀ (female)" package=THT]
  Part1 = Franzininho WiFi

nets:
  N1: GY1.pin1, Part1.3V3
  N2: GY1.pin2, Part1.GND#19
  N3: GY1.pin3, Part1.9
  N4: GY1.pin4, Part1.8

custom parts:
  GY-521 (MPU-6050): Placa GY-521 basada en conjunto de acelerómetro+giroscopios MPU-6050
  Franzininho WiFi: Placa de desenvolvimento ESP32-S2
