# Fritzing sketch FranzininhoWiFi_USB_HID_Keyboard_Fritzing (saved by Fritzing 0.9.6b)
breadboards: 1

parts:
  Part1 = Franzininho WiFi
  S1 = Pushbutton [package="[THT]"]

nets:
  N1: Part1.3, S1.Pin_3, S1.Pin_4
  N2: Part1.GND#19, S1.Pin_1, S1.Pin_2

custom parts:
  Franzininho WiFi: Placa de desenvolvimento ESP32-S2
