# Fritzing sketch FranzininhoWiFi_WebServer_Fritzing (saved by Fritzing 0.9.6b)
breadboards: 1

parts:
  Part1 = Franzininho WiFi
  R1 = Photocell (LDR) [package=THT]
  R2 = Resistor [tolerance=±5% power=0.25 resistance=10k package=THT]

nets:
  N1: Part1.3, R1.pin_0, R2.Pin_0

custom parts:
  Franzininho WiFi: Placa de desenvolvimento ESP32-S2
